# Fritzing sketch Circuit schematic (saved by Fritzing 0.9.3b)
breadboards: 1

parts:
  Part1 = Arduino Uno (Rev3)
  SG1 = Buzzer 12mm [package=buzzer-12mm-ns]
  LED1 = LED - 5mm [color="Red (633nm)" package="5 mm [THT]"]
  R1 = Resistor [tolerance=±5% resistance=220 package=THT]
  R2 = Resistor [tolerance=±5% resistance=220 package=THT]
  R3 = Photocell (LDR) [package=THT]
  S1 = Momentary Switch [package=ksa_sealed_tac_switch]
  R4 = Resistor [tolerance=±5% resistance=220 package=THT]
  T1 = LM35 Temperature Sensor [package="TO92 [THT]"]
  J1 = Basic Servo
  HC-SR04_Sensor_1 = HC-SR04 Ultrasonic Distance Sensor
  M1 = pcf8574 io expansion board [package=THT]
  Part2 = LCD1602-I2C
  U1 = NodeMCU V1.0

nets:
  N1: Part1.A0, T1.Vout
  N2: Part1.A1, R2.Pin_1, R3.pin_0
  N3: Part1.A2, S1.3, S1.4, R4.Pin_1
  GND: Part1.GND, R3.pin_1, R4.Pin_0, J1.gnd, HC-SR04_Sensor_1.GND, M1.GND, Part2.GND
  N4: Part1.A4/SDA, M1.SDA, Part2.SDA
  N5: Part1.A5/SCL, M1.SCL, Part2.SCL
  N6: Part1.D0/RX, U1.TX
  N7: Part1.D1/TX, U1.RX
  N8: Part1.D2, J1.pulse
  N9: Part1.D3_PWM, SG1.2
  N10: Part1.D4, R1.Pin_0
  N11: Part1.D5_PWM, HC-SR04_Sensor_1.TRIG
  N12: Part1.D6_PWM, HC-SR04_Sensor_1.ECHO
  VCC: Part1.5V, R2.Pin_0, S1.1, S1.2, T1.+Vs, J1.vcc, HC-SR04_Sensor_1.VCC, M1.VCC, Part2.VCC
  N13: SG1.1, LED1.cathode, T1.GND
  N14: LED1.anode, R1.Pin_1

custom parts:
  pcf8574 io expansion board: pcf8574 io expansion board.
  LCD1602-I2C: A standard character display, usually with 2x16 characters. Comes in many colors with LCM1602 IIC attached.
  NodeMCU V1.0: ESP8266 based NodeMCU
